// Logisim project miniCurso.circ as structural Verilog: 3 circuits, main circuit main
module main (
  input  A,
  input  B,
  output Cin,
  output SomaAB
);

  and and_1 (Cin, A, B);
  xor xor_1 (SomaAB, A, B);
endmodule

module HalfAdder (
  input  A,
  input  B,
  output Cin,
  output SomaAB
);

  and and_1 (Cin, A, B);
  xor xor_1 (SomaAB, A, B);
endmodule

module FullAdder (
  input  A,
  input  B,
  input  Cin,
  output CO1,
  output Cout,
  output S1,
  output CO2,
  output S
);

  and and_1 (CO1, A, B);
  xor xor_1 (S1, A, B);
  xor xor_2 (S, S1, Cin);
  and and_2 (CO2, S1, Cin);
  or or_1 (Cout, CO1, CO2);
endmodule
